# Fritzing sketch programmer (saved by Fritzing 0.8.5b)
breadboards: 1

parts:
  Bauteil1 = Arduino Uno (Rev3)
  U1 = attiny85 [package=dip]
  C1 = Electrolytic Capacitor [capacitance=10µF package="100 mil [THT, electrolytic]"]

nets:
  N1: Bauteil1.D10_PWM/SS, U1.Pin_1
  N2: Bauteil1.D11_PWM/MOSI, U1.Pin_5
  N3: Bauteil1.D12/MISO, U1.Pin_6
  N4: Bauteil1.D13/SCK, U1.Pin_7
  N5: Bauteil1.GND, U1.Pin_4, C1.-
  N6: Bauteil1.RESET, C1.+
  N7: Bauteil1.5V, U1.Pin_8

notes:
  To program a Attiny 45 85 you need:
  - Arduino IDE 0.22 (current 1.0.5 does not work)
  - this hardware library http://highlowtech.org/?p=1229
  (also in the repo. Thanks highlowtech group)
  - a 10uf capacitor for preventing reset on programming
  See the tutorials on how to set it up @ http://highlowtech.org/?p=1229
